// Logisim project y86.circ as structural Verilog: 3 circuits, main circuit main
module main (
  input  Reset
);

  wire and_1_out, Clock_out, nor_1_out, not_1_out;
  wire [1:0] imem_1_p2, Stat_q;
  wire [31:0] PC_q, PChold_q;

  and and_1 (and_1_out, Clock_out, nor_1_out);
  Clock Clock (.out(Clock_out));
  Register #(.width(32)) PC (.D(PChold_q), .Q(PC_q), .clk(and_1_out), .clr(Reset));  // open: en
  nor nor_1 (nor_1_out, Stat_q[1], Stat_q[0]);
  not not_1 (not_1_out, and_1_out);
  Register #(.width(2)) Stat (.D(imem_1_p2), .Q(Stat_q), .clk(not_1_out));  // open: en, clr
  // imem imem_1: pin names not known; wires that end beside it: PC_q, imem_1_p2
  Register #(.width(32)) PChold (.Q(PChold_q), .clk(not_1_out), .clr(Reset));  // open: D, en
endmodule

module Align (
  input  [7:0] B1,
  input  [7:0] B2,
  input  [7:0] B3,
  input  [7:0] B4,
  input  [7:0] B5,
  input  [7:0] B6,
  input  [7:0] B7,
  input  [7:0] B8,
  input  [7:0] B9,
  input  NeedRegs,
  output [3:0] rA,
  output [3:0] rB,
  output [31:0] valC_1,
  output [31:0] valC_0
);
endmodule

module Fetch (
  input  [7:0] in_1,
  input  [7:0] in_2,
  input  [7:0] in_3,
  input  [7:0] in_4,
  input  [7:0] in_5,
  input  [7:0] in_6,
  input  [7:0] in_7,
  input  [7:0] in_8,
  input  [7:0] in_9,
  input  [7:0] in_10,
  output [3:0] out_11,
  output [3:0] out_12
);

  Align align_1 (
    .B1(in_2), .B2(in_3), .B3(in_4), .B4(in_5), .B5(in_6), .B6(in_7), .B7(in_8), .B8(in_9), .B9(in_10));  // open: NeedRegs, rA, rB, valC_1, valC_0

  assign out_11 = in_1[3:0];
  assign out_12 = in_1[7:4];
endmodule
